// Logisim project nibadder.circ as structural Verilog: 1 circuit, main circuit main
module main (
  input  cin0,
  input  [3:0] inputA,
  input  [3:0] inputB,
  output [3:0] AplusB,
  output CFlag
);

  wire a0andb0_out, a1andb1_out, cin0a0_out, cin0anda0_out, cin0b0_out, cin1a1_out, cin1anda1_out,
       cin1b1_out, cin2a2_out, cin2anda2_out, cin2andb2_out, cin2b2_out, cin3a3_out, cin3anda3_out,
       cin3andb3_out, cin3b3_out, or_1_out, or_2_out, or_3_out;

  xor cin2a2 (cin2a2_out, or_3_out, inputA[2]);
  and cin2b2 (cin2b2_out, or_3_out, inputB[2]);
  and cin2anda2 (cin2anda2_out, or_3_out, inputA[2]);
  and cin2andb2 (cin2andb2_out, inputA[2], inputB[2]);
  and cin0b0 (cin0b0_out, cin0, inputB[0]);
  and cin0anda0 (cin0anda0_out, cin0, inputA[0]);
  and a0andb0 (a0andb0_out, inputA[0], inputB[0]);
  xor cin1a1 (cin1a1_out, or_2_out, inputA[1]);
  and cin1b1 (cin1b1_out, or_2_out, inputB[1]);
  and cin1anda1 (cin1anda1_out, or_2_out, inputA[1]);
  and a1andb1 (a1andb1_out, inputA[1], inputB[1]);
  xor xor_1 (AplusB[2], cin2a2_out, inputB[2]);
  or or_1 (or_1_out, cin2b2_out, cin2anda2_out, cin2andb2_out);
  xor cin3a3 (cin3a3_out, or_1_out, inputA[3]);
  and cin3b3 (cin3b3_out, or_1_out, inputB[3]);
  and cin3anda3 (cin3anda3_out, or_1_out, inputA[3]);
  and cin3andb3 (cin3andb3_out, inputA[3], inputB[3]);
  xor cin0a0 (cin0a0_out, cin0, inputA[0]);
  xor xor_2 (AplusB[0], cin0a0_out, inputB[0]);
  or or_2 (or_2_out, cin0b0_out, cin0anda0_out, a0andb0_out);
  xor xor_3 (AplusB[1], cin1a1_out, inputB[1]);
  or or_3 (or_3_out, cin1b1_out, cin1anda1_out, a1andb1_out);
  xor xor_4 (AplusB[3], cin3a3_out, inputB[3]);
  or or_4 (CFlag, cin3b3_out, cin3anda3_out, cin3andb3_out);

  // Notes on the sheet:
  //   a[0]
  //   a[1]
  //   a[2]
  //   b[0]
  //   b[3]
  //   a[3]
  //   cin1
  //   b[1]
  //   b[2]
  //   Isabel Sutedjo I pledge my honor that I have abided by the Stevens Honor System.
  //   s[2]
  //   cout[2]
  //   s[0]
  //   s[1]
  //   s[3]
  //   cout[3]
  //   cout[0]
  //   cout[1]
endmodule
