// Logisim project nibmux.circ as structural Verilog: 1 circuit, main circuit main
module main (
  input  Switch,
  input  [3:0] inputA,
  input  [3:0] inputB,
  output [3:0] AorB
);

  wire notGate_out, switcha0_out, switcha1_out, switcha2_out, switcha3_out, switchb0_out, switchb1_out,
       switchb2_out, switchb3_out;

  not notGate (notGate_out, Switch);
  and switcha0 (switcha0_out, notGate_out, inputA[0]);
  and switchb0 (switchb0_out, Switch, inputB[0]);
  and switcha1 (switcha1_out, notGate_out, inputA[1]);
  or output1 (AorB[1], switcha1_out, switchb1_out);
  and switchb1 (switchb1_out, Switch, inputB[1]);
  and switcha2 (switcha2_out, notGate_out, inputA[2]);
  and switchb2 (switchb2_out, Switch, inputB[2]);
  and switcha3 (switcha3_out, notGate_out, inputA[3]);
  and switchb3 (switchb3_out, Switch, inputB[3]);
  or output0 (AorB[0], switcha0_out, switchb0_out);
  or output2 (AorB[2], switcha2_out, switchb2_out);
  or output3 (AorB[3], switcha3_out, switchb3_out);

  // Notes on the sheet:
  //   Isabel Sutedjo I pledge my honor that I have abided by the Stevens Honor System.
endmodule
