// Logisim project miniRegister.circ as structural Verilog: 1 circuit, main circuit main
module main (
  input  [1:0] writeReg,
  input  regWrite,
  input  [1:0] readReg1,
  input  [7:0] regDataW,
  input  [1:0] readReg2,
  output [7:0] regData1,
  output [7:0] regData2
);

  wire and_1_out, and_2_out, and_3_out, and_4_out, c_out, decoder_1_out0, decoder_1_out1, decoder_1_out2,
       decoder_1_out3;
  wire [7:0] X0_q, X1_q, X2_q, X3_q;

  Decoder #(.select(2)) decoder_1 (
    .out0(decoder_1_out0), .out1(decoder_1_out1), .out2(decoder_1_out2), .out3(decoder_1_out3), .sel(writeReg));  // open: en
  and and_1 (and_1_out, regWrite, decoder_1_out0);
  and and_2 (and_2_out, regWrite, decoder_1_out1);
  Clock c (.out(c_out));
  and and_3 (and_3_out, regWrite, decoder_1_out2);
  and and_4 (and_4_out, regWrite, decoder_1_out3);
  Register X0 (.D(regDataW), .en(and_1_out), .clk(c_out), .Q(X0_q));  // open: clr
  Register X1 (.D(regDataW), .en(and_2_out), .clk(c_out), .Q(X1_q));  // open: clr
  Register X2 (.D(regDataW), .en(and_3_out), .clk(c_out), .Q(X2_q));  // open: clr
  Register X3 (.D(regDataW), .en(and_4_out), .clk(c_out), .Q(X3_q));  // open: clr
  Multiplexer #(.select(2), .width(8)) multiplexer_1 (
    .in0(X0_q), .in1(X1_q), .in2(X2_q), .in3(X3_q), .out(regData1), .sel(readReg1));
  Multiplexer #(.select(2), .width(8)) multiplexer_2 (
    .in0(X0_q), .in1(X1_q), .in2(X2_q), .in3(X3_q), .out(regData2), .sel(readReg2));

  // Notes on the sheet:
  //   Isabel Sutedjo I pledge my honor that I have abided by the Stevens Honor System.
endmodule
