// Logisim project memory.circ as structural Verilog: 1 circuit, main circuit main
module main (
  output [7:0] outputPin
);

  wire clock_1_out;
  wire [7:0] adder_1_out, aRegister_q;

  Clock clock_1 (.out(clock_1_out));
  Adder adder_1 (.a(8'h1), .b(aRegister_q), .out(adder_1_out));  // open: cin, cout
  Register aRegister (.D(adder_1_out), .clk(clock_1_out), .Q(aRegister_q));  // open: en, clr
  RAM ram_1 (.addr(aRegister_q), .we(1'b0), .oe(1'b1), .clk(clock_1_out), .dout(outputPin));  // open: din

  // Notes on the sheet:
  //   left side - write
  //   Isabel Sutedjo I pledge my honor that I have abided by the Stevens Honor System.
  //   right side - read
endmodule
